// Logisim project CPUproject.circ as structural Verilog: 8 circuits, main circuit main
module main (
  output overflow,
  output zero,
  output negative
);

  wire a, address, ALU_o0, ALU_o1, ALU_o2, ALU_o3, and_2_out, and_3_out, and_4_out, and_5_out, and_6_out,
       and_7_out, and_8_out, and_9_out, and_10_out, and_11_out, and_12_out, and_13_out, and_14_out,
       and_15_out, and_16_out, and_17_out, and_18_out, and_19_out, and_20_out, and_21_out, and_22_out,
       and_23_out, and_24_out, and_25_out, and_26_out, and_27_out, and_28_out, and_29_out, and_30_out,
       and_31_out, and_32_out, and_33_out, and_34_out, and_35_out, and_36_out, and_37_out, and_38_out, bit0,
       bit1, bit2, bit3, clk, clock_1_out, Control_Unit_halt, D_o0, D_o1, D_o2, D_o3, enable, halt, INC_o0,
       INC_o1, INC_o2, IR_o0, IR_o1, IR_o2, IR_o3, iren, load, MAR_o0, MAR_o1, MAR_o2, maren, MBR_o0, MBR_o1,
       MBR_o2, MBR_o3, mbren, not_1_out, not_2_out, not_3_out, not_4_out, not_5_out, not_6_out, not_7_out,
       not_8_out, not_9_out, numbers_1_eight, numbers_1_eleven, numbers_1_fifteen, numbers_1_five,
       numbers_1_four, numbers_1_fourteen, numbers_1_nine, numbers_1_one, numbers_1_seven, numbers_1_six,
       numbers_1_ten, numbers_1_thirteen, numbers_1_three, numbers_1_twelve, numbers_1_two, numbers_1_zero,
       op, or_1_out, or_2_out, or_3_out, or_4_out, or_5_out, or_6_out, or_7_out, or_8_out, or_9_out,
       or_10_out, or_11_out, or_12_out, or_13_out, or_14_out, or_15_out, or_16_out, or_17_out, or_18_out,
       or_19_out, or_20_out, or_21_out, or_22_out, or_23_out, or_24_out, or_25_out, or_26_out, or_27_out,
       or_28_out, or_29_out, or_30_out, or_31_out, or_32_out, or_33_out, or_34_out, or_35_out, PC_o0, PC_o1,
       PC_o2, pcen, put, r0, R0_o0, R0_o1, R0_o2, R0_o3, r1, R1_o0, R1_o1, R1_o2, R1_o3, RAM_o0, RAM_o1,
       RAM_o2, RAM_o3, rammode, s, save;

  and and_1 (clk, halt, clock_1_out);
  or or_1 (or_1_out, MAR_o1, and_2_out);
  not not_1 (not_1_out, address);
  and and_2 (and_2_out, save, address);
  Clock clock_1 (.out(clock_1_out));
  or or_2 (or_2_out, MAR_o0, and_3_out);
  and and_3 (and_3_out, not_1_out, save);
  not not_2 (not_2_out, save);
  and and_4 (and_4_out, MAR_o2, not_2_out);
  not not_3 (not_3_out, enable);
  and and_5 (and_5_out, save, R1_o3);
  and and_6 (and_6_out, save, R1_o2);
  and and_7 (and_7_out, save, R1_o1);
  and and_8 (and_8_out, save, R1_o0);
  and and_9 (and_9_out, save, R0_o3);
  and and_10 (and_10_out, save, R0_o2);
  and and_11 (and_11_out, save, R0_o1);
  and and_12 (and_12_out, save, R0_o0);
  not not_4 (not_4_out, rammode);
  or or_3 (or_3_out, and_5_out, and_9_out);
  or or_4 (or_4_out, and_6_out, and_10_out);
  ramProf RAM (
    .A2(and_4_out), .A1(or_1_out), .A0(or_2_out), .Mode(not_4_out), .D3(and_23_out), .D2(and_21_out),
    .D1(and_22_out), .D0(and_20_out), .enable(not_3_out), .O3(RAM_o3), .O2(RAM_o2), .O1(RAM_o1), .O0(RAM_o0),
    .bit3(bit3), .bit2(bit2), .bit1(bit1), .bit0(bit0));
  or or_5 (or_5_out, and_7_out, and_11_out);
  or or_6 (or_6_out, and_8_out, and_12_out);
  or or_7 (or_7_out, RAM_o3, or_3_out);
  or or_8 (or_8_out, RAM_o2, or_4_out);
  or or_9 (or_9_out, RAM_o1, or_5_out);
  or or_10 (or_10_out, RAM_o0, or_6_out);
  and and_13 (and_13_out, and_15_out, RAM_o3);
  and and_14 (and_14_out, and_15_out, RAM_o1);
  and and_15 (and_15_out, r1, and_19_out);
  and and_16 (and_16_out, r1, op);
  reg3bits MAR (.rw(maren), .enable(1'b1), .I2(PC_o2), .I1(PC_o1), .I0(PC_o0), .O2(MAR_o2), .O1(MAR_o1), .O0(MAR_o0));
  and and_17 (and_17_out, and_15_out, RAM_o2);
  and and_18 (and_18_out, and_15_out, RAM_o0);
  and and_19 (and_19_out, load, put);
  and and_20 (and_20_out, MBR_o0, save);
  reg4bits MBR (
    .rw(mbren), .enable(1'b1), .I3(or_7_out), .I2(or_8_out), .I1(or_9_out), .I0(or_10_out), .O3(MBR_o3),
    .O2(MBR_o2), .O1(MBR_o1), .O0(MBR_o0));
  and and_21 (and_21_out, MBR_o2, save);
  and and_22 (and_22_out, MBR_o1, save);
  reg4bits u_R1 (
    .rw(and_15_out), .enable(1'b1), .I3(and_13_out), .I2(and_17_out), .I1(and_14_out), .I0(and_18_out),
    .O3(R1_o3), .O2(R1_o2), .O1(R1_o1), .O0(R1_o0));
  and and_23 (and_23_out, MBR_o3, save);
  and and_24 (and_24_out, and_16_out, R1_o3);
  and and_25 (and_25_out, and_16_out, R1_o2);
  and and_26 (and_26_out, and_16_out, R1_o1);
  and and_27 (and_27_out, and_16_out, R1_o0);
  and and_28 (and_28_out, and_32_out, RAM_o3);
  and and_29 (and_29_out, and_32_out, RAM_o2);
  and and_30 (and_30_out, and_32_out, RAM_o1);
  and and_31 (and_31_out, and_32_out, RAM_o0);
  and and_32 (and_32_out, r0, and_33_out);
  and and_33 (and_33_out, put, load);
  not not_5 (not_5_out, 1'b1);
  not not_6 (not_6_out, 1'b1);
  not not_7 (not_7_out, 1'b1);
  or or_11 (or_11_out, and_28_out, ALU_o3);
  not not_8 (not_8_out, 1'b1);
  or or_12 (or_12_out, op, and_32_out);
  or or_13 (or_13_out, and_29_out, ALU_o2);
  or or_14 (or_14_out, and_30_out, ALU_o1);
  or or_15 (or_15_out, and_31_out, ALU_o0);
  and and_34 (and_34_out, r0, op);
  reg3bits PC (.rw(pcen), .enable(pcen), .I2(INC_o2), .I1(INC_o1), .I0(INC_o0), .O2(PC_o2), .O1(PC_o1), .O0(PC_o0));
  reg4bits IR (
    .rw(iren), .enable(1'b1), .I3(MBR_o3), .I2(MBR_o2), .I1(MBR_o1), .I0(MBR_o0), .O3(IR_o3), .O2(IR_o2),
    .O1(IR_o1), .O0(IR_o0));
  and and_35 (and_35_out, and_34_out, R0_o3);
  and and_36 (and_36_out, and_34_out, R0_o2);
  and and_37 (and_37_out, and_34_out, R0_o1);
  and and_38 (and_38_out, and_34_out, R0_o0);
  or or_16 (or_16_out, and_25_out, and_36_out);
  reg4bits u_R0 (
    .rw(or_12_out), .enable(1'b1), .I3(or_11_out), .I2(or_13_out), .I1(or_14_out), .I0(or_15_out),
    .O3(R0_o3), .O2(R0_o2), .O1(R0_o1), .O0(R0_o0));
  or or_17 (or_17_out, and_24_out, and_35_out);
  or or_18 (or_18_out, and_26_out, and_37_out);
  aluS INC (
    .L3(not_5_out), .L2(not_6_out), .L1(not_7_out), .L0(1'b1), .R2(PC_o2), .R1(PC_o1), .R0(PC_o0),
    .command_pin(not_8_out), .O2(INC_o2), .O1(INC_o1), .O0(INC_o0));  // open: R3, overflow_status_bit, zero_status_bit, negative_status_bit, O3
  or or_19 (or_19_out, and_27_out, and_38_out);
  CU Control_Unit (
    .OP1(IR_o1), .OP0(IR_o0), .regIn(IR_o2), .addressIn(IR_o3), .halt(Control_Unit_halt), .load(load),
    .addressOut(address), .maren(maren), .rammode(rammode), .mbren(mbren), .PCen(pcen), .put(put),
    .save(save), .iren(iren), .a(a), .operation(op), .s(s), .regOut(r1), .enable(enable));
  not not_9 (not_9_out, s);
  not not_10 (halt, Control_Unit_halt);
  not not_11 (r0, r1);
  or or_20 (or_20_out, a, not_9_out);
  aluS ALU (
    .L3(R0_o3), .L2(R0_o2), .L1(R0_o1), .L0(R0_o0), .R3(or_17_out), .R2(or_16_out), .R1(or_18_out),
    .R0(or_19_out), .command_pin(or_20_out), .overflow_status_bit(overflow), .zero_status_bit(zero),
    .negative_status_bit(negative), .O3(ALU_o3), .O2(ALU_o2), .O1(ALU_o1), .O0(ALU_o0));
  or or_21 (or_21_out, numbers_1_five, numbers_1_zero, numbers_1_one, numbers_1_four, numbers_1_fourteen, numbers_1_six, numbers_1_eight, numbers_1_nine, numbers_1_ten);
  or or_22 (or_22_out, numbers_1_zero, numbers_1_two, numbers_1_three, numbers_1_five, numbers_1_ten, numbers_1_six, numbers_1_seven, numbers_1_eight, numbers_1_nine);
  reg4bits D (
    .rw(1'b1), .enable(1'b1), .I3(bit3), .I2(bit2), .I1(bit1), .I0(bit0), .O3(D_o3), .O2(D_o2), .O1(D_o1),
    .O0(D_o0));
  or or_23 (or_23_out, numbers_1_four, numbers_1_zero, numbers_1_two, numbers_1_three, numbers_1_eleven, numbers_1_seven, numbers_1_eight, numbers_1_nine, numbers_1_ten);
  or or_24 (or_24_out, numbers_1_two, numbers_1_three, numbers_1_four, numbers_1_five, numbers_1_twelve, numbers_1_six, numbers_1_eight, numbers_1_nine);
  or or_25 (or_25_out, numbers_1_two, numbers_1_zero, numbers_1_one, numbers_1_twelve, numbers_1_six, numbers_1_eight, numbers_1_ten);
  or or_26 (or_26_out, numbers_1_zero, numbers_1_two, numbers_1_three, numbers_1_ten, numbers_1_five, numbers_1_six, numbers_1_eight);
  _7_Segment_Display u_7_segment_display_1 (.b(or_32_out), .c(or_33_out));  // open: g, f, a, e, d, dp
  numbers numbers_1 (
    .I3(D_o3), .I2(D_o2), .I1(D_o1), .I0(D_o0), .fifteen(numbers_1_fifteen), .fourteen(numbers_1_fourteen),
    .thirteen(numbers_1_thirteen), .twelve(numbers_1_twelve), .eleven(numbers_1_eleven), .ten(numbers_1_ten),
    .nine(numbers_1_nine), .eight(numbers_1_eight), .seven(numbers_1_seven), .six(numbers_1_six),
    .five(numbers_1_five), .four(numbers_1_four), .three(numbers_1_three), .two(numbers_1_two),
    .one(numbers_1_one), .zero(numbers_1_zero));
  or or_27 (or_27_out, numbers_1_zero, numbers_1_three, numbers_1_four, numbers_1_five, numbers_1_ten, numbers_1_six, numbers_1_seven, numbers_1_eight, numbers_1_nine);
  or or_28 (or_28_out, or_24_out, numbers_1_thirteen, numbers_1_fifteen, numbers_1_fourteen);
  _7_Segment_Display u_7_segment_display_2 (
    .g(or_28_out), .f(or_30_out), .a(or_35_out), .b(or_31_out), .e(or_25_out), .d(or_29_out), .c(or_34_out));  // open: dp
  or or_29 (or_29_out, or_26_out, numbers_1_twelve, numbers_1_thirteen, numbers_1_fifteen);
  or or_30 (or_30_out, or_21_out, numbers_1_fifteen);
  or or_31 (or_31_out, or_23_out, numbers_1_fourteen, numbers_1_thirteen, numbers_1_twelve);
  or or_32 (or_32_out, numbers_1_ten, numbers_1_eleven, numbers_1_twelve, numbers_1_thirteen, numbers_1_fourteen, numbers_1_fifteen);
  or or_33 (or_33_out, numbers_1_ten, numbers_1_eleven, numbers_1_twelve, numbers_1_thirteen, numbers_1_fourteen, numbers_1_fifteen);
  or or_34 (or_34_out, or_27_out, numbers_1_eleven, numbers_1_thirteen, numbers_1_fourteen, numbers_1_fifteen);
  or or_35 (or_35_out, numbers_1_twelve, numbers_1_thirteen, numbers_1_fifteen, or_22_out);

  // Notes on the sheet:
  //   STUDENT 1: SAAD RAHMAN
  //   STUDENT ID: 260949400
  //   STUDENT 2: MICHEL HIJAZIN 
  //   STUDENT ID: 261002509 
  //   U BUS
endmodule

module reg4bits (
  input  rw,
  input  enable,
  input  I3,
  input  I2,
  input  I1,
  input  I0,
  output O3,
  output O2,
  output O1,
  output O0
);

  wire and_1_out, clk_out, d_ff_1_q, d_ff_2_q, d_ff_3_q, d_ff_4_q;

  Clock clk (.out(clk_out));
  and and_1 (and_1_out, clk_out, rw);
  D_Flip_Flop #(.trigger("falling")) d_ff_1 (.D(I0), .clk(and_1_out), .Q(d_ff_1_q));  // open: Qn, preset, reset
  D_Flip_Flop #(.trigger("falling")) d_ff_2 (.D(I1), .clk(and_1_out), .Q(d_ff_2_q));  // open: Qn, preset, reset
  D_Flip_Flop #(.trigger("falling")) d_ff_3 (.D(I2), .clk(and_1_out), .Q(d_ff_3_q));  // open: Qn, preset, reset
  D_Flip_Flop #(.trigger("falling")) d_ff_4 (.D(I3), .clk(and_1_out), .Q(d_ff_4_q));  // open: Qn, preset, reset
  and and_2 (O0, d_ff_1_q, enable);
  and and_3 (O1, d_ff_2_q, enable);
  and and_4 (O2, d_ff_3_q, enable);
  and and_5 (O3, d_ff_4_q, enable);

  // Notes on the sheet:
  //   1: write
  //   0: read
endmodule

module aluS (
  input  L3,
  input  L2,
  input  L1,
  input  L0,
  input  R3,
  input  R2,
  input  R1,
  input  R0,
  input  command_pin,
  output overflow_status_bit,
  output zero_status_bit,
  output negative_status_bit,
  output O3,
  output O2,
  output O1,
  output O0
);

  wire and_1_out, and_2_out, and_3_out, and_4_out, and_5_out, and_6_out, and_7_out, and_8_out, and_9_out,
       and_10_out, and_11_out, and_12_out, and_13_out, and_14_out, and_15_out, and_16_out, and_17_out,
       and_18_out, and_19_out, and_20_out, and_21_out, and_22_out, and_23_out, and_24_out, and_25_out,
       and_26_out, and_28_out, and_29_out, and_30_out, and_31_out, clock_1_out, not_1_out, not_2_out,
       not_3_out, not_4_out, not_5_out, not_6_out, not_7_out, not_8_out, or_1_out, or_2_out, or_3_out,
       or_4_out, or_5_out, or_6_out, or_8_out, or_9_out, or_10_out, xor_2_out, xor_3_out, xor_4_out,
       xor_8_out, xor_9_out, xor_10_out, xor_11_out, xor_12_out, xor_13_out, xor_14_out;

  not not_1 (not_1_out, command_pin);
  Clock clock_1 (.out(clock_1_out));
  and and_1 (and_1_out, clock_1_out, L3);
  and and_2 (and_2_out, clock_1_out, L2);
  and and_3 (and_3_out, clock_1_out, L1);
  and and_4 (and_4_out, L0, clock_1_out);
  and and_5 (and_5_out, clock_1_out, or_1_out);
  and and_6 (and_6_out, R3, not_1_out);
  or or_1 (or_1_out, and_6_out, and_31_out);
  and and_7 (and_7_out, clock_1_out, or_2_out);
  and and_8 (and_8_out, R2, not_1_out);
  and and_9 (and_9_out, clock_1_out, or_3_out);
  and and_10 (and_10_out, R1, not_1_out);
  or or_2 (or_2_out, and_8_out, and_30_out);
  and and_11 (and_11_out, R0, not_1_out);
  or or_3 (or_3_out, and_10_out, and_29_out);
  or or_4 (or_4_out, and_11_out, and_28_out);
  and and_12 (and_12_out, clock_1_out, or_4_out);
  not not_2 (not_2_out, R3);
  not not_3 (not_3_out, R2);
  not not_4 (not_4_out, R1);
  not not_5 (not_5_out, R0);
  xor xor_1 (O0, and_12_out, and_4_out);
  and and_13 (and_13_out, and_12_out, and_4_out);
  not not_6 (not_6_out, 1'b1);
  not not_7 (not_7_out, 1'b1);
  and and_14 (and_14_out, and_9_out, and_3_out);
  and and_15 (and_15_out, and_7_out, and_2_out);
  xor xor_2 (xor_2_out, and_7_out, and_2_out);
  and and_16 (and_16_out, and_5_out, and_1_out);
  not not_8 (not_8_out, 1'b1);
  xor xor_3 (xor_3_out, and_9_out, and_3_out);
  xor xor_4 (xor_4_out, and_5_out, and_1_out);
  xor xor_5 (O1, xor_3_out, and_13_out);
  and and_17 (and_17_out, xor_3_out, and_13_out);
  xor xor_6 (O2, xor_2_out, or_5_out);
  and and_18 (and_18_out, xor_2_out, or_5_out);
  xor xor_7 (negative_status_bit, xor_4_out, or_6_out);
  and and_19 (and_19_out, xor_4_out, or_6_out);
  or or_5 (or_5_out, and_14_out, and_17_out);
  or or_6 (or_6_out, and_15_out, and_18_out);
  or or_7 (overflow_status_bit, and_16_out, and_19_out);
  xor xor_8 (xor_8_out, not_5_out, 1'b1);
  and and_20 (and_20_out, not_5_out, 1'b1);
  and and_21 (and_21_out, not_4_out, not_8_out);
  xor xor_9 (xor_9_out, not_4_out, not_8_out);
  and and_22 (and_22_out, not_7_out, not_3_out);
  xor xor_10 (xor_10_out, not_7_out, not_3_out);
  and and_23 (and_23_out, not_6_out, not_2_out);
  xor xor_11 (xor_11_out, not_6_out, not_2_out);
  xor xor_12 (xor_12_out, xor_9_out, and_20_out);
  and and_24 (and_24_out, xor_9_out, and_20_out);
  xor xor_13 (xor_13_out, xor_10_out, or_8_out);
  and and_25 (and_25_out, xor_10_out, or_8_out);
  xor xor_14 (xor_14_out, xor_11_out, or_9_out);
  and and_26 (and_26_out, xor_11_out, or_9_out);
  or or_8 (or_8_out, and_21_out, and_24_out);
  or or_9 (or_9_out, and_22_out, and_25_out);
  or or_10 (or_10_out, and_23_out, and_26_out);
  and and_27 (zero_status_bit, ~negative_status_bit, ~O2, ~O1, ~O0);  // AND_Gate
  and and_28 (and_28_out, command_pin, xor_8_out);
  and and_29 (and_29_out, xor_12_out, command_pin);
  and and_30 (and_30_out, xor_13_out, command_pin);
  and and_31 (and_31_out, xor_14_out, command_pin);

  assign O3 = negative_status_bit;

  // Notes on the sheet:
  //   clock
  //   L
  //   R 
  //   carry
  //   output
  //   carry
endmodule

module reg3bits (
  input  rw,
  input  enable,
  input  I2,
  input  I1,
  input  I0,
  output O2,
  output O1,
  output O0
);

  wire and_1_out, clk_out, d_ff_1_q, d_ff_2_q, d_ff_3_q;

  Clock clk (.out(clk_out));
  and and_1 (and_1_out, clk_out, rw);
  D_Flip_Flop #(.trigger("falling")) d_ff_1 (.D(I0), .clk(and_1_out), .Q(d_ff_1_q));  // open: Qn, preset, reset
  D_Flip_Flop #(.trigger("falling")) d_ff_2 (.D(I1), .clk(and_1_out), .Q(d_ff_2_q));  // open: Qn, preset, reset
  D_Flip_Flop #(.trigger("falling")) d_ff_3 (.D(I2), .clk(and_1_out), .Q(d_ff_3_q));  // open: Qn, preset, reset
  and and_2 (O0, d_ff_1_q, enable);
  and and_3 (O1, d_ff_2_q, enable);
  and and_4 (O2, d_ff_3_q, enable);

  // Notes on the sheet:
  //   1: write
  //   0: read
endmodule

module ramProf (
  input  A2,
  input  A1,
  input  A0,
  input  Mode,
  input  D3,
  input  D2,
  input  D1,
  input  D0,
  input  enable,
  output O3,
  output O2,
  output O1,
  output O0,
  output bit3,
  output bit2,
  output bit1,
  output bit0
);

  wire and_1_out, and_2_out, and_3_out, and_4_out, and_5_out, and_6_out, and_7_out, and_8_out, and_9_out,
       and_10_out, and_11_out, and_12_out, and_13_out, and_14_out, and_15_out, and_16_out, and_17_out,
       and_18_out, and_19_out, and_20_out, and_21_out, and_22_out, and_23_out, and_24_out, and_25_out,
       and_26_out, and_27_out, and_28_out, and_29_out, and_30_out, and_31_out, and_32_out, and_33_out,
       and_34_out, and_35_out, and_36_out, and_37_out, and_38_out, and_39_out, and_40_out, and_41_out,
       and_42_out, and_43_out, and_44_out, and_45_out, and_46_out, and_47_out, and_48_out, and_49_out,
       and_50_out, and_51_out, and_52_out, and_53_out, and_54_out, and_55_out, and_56_out, and_57_out,
       and_58_out, and_59_out, and_60_out, and_61_out, and_62_out, and_63_out, and_64_out, and_65_out,
       and_66_out, and_67_out, and_68_out, and_69_out, and_70_out, and_71_out, and_72_out, and_73_out,
       and_74_out, and_75_out, and_76_out, and_77_out, and_78_out, and_79_out, and_80_out, clock_1_out,
       d_ff_1_q, d_ff_2_q, d_ff_3_q, d_ff_4_q, d_ff_5_q, d_ff_6_q, d_ff_7_q, d_ff_8_q, d_ff_9_q, d_ff_10_q,
       d_ff_11_q, d_ff_13_q, d_ff_14_q, d_ff_15_q, d_ff_16_q, d_ff_17_q, d_ff_18_q, d_ff_19_q, d_ff_20_q,
       d_ff_21_q, d_ff_23_q, d_ff_24_q, d_ff_25_q, d_ff_26_q, d_ff_27_q, d_ff_28_q, d_ff_29_q, d_ff_30_q,
       d_ff_31_q, d_ff_32_q, d_ff_33_q, d_ff_34_q, d_ff_35_q, d_ff_37_q, d_ff_38_q, d_ff_39_q, d_ff_40_q,
       d_ff_41_q, d_ff_42_q, d_ff_43_q, not_1_out, not_2_out, not_3_out, not_4_out, not_5_out, not_6_out,
       not_7_out, not_8_out, not_9_out, not_10_out, not_11_out, not_12_out, not_13_out, or_1_out, or_2_out,
       or_3_out, or_4_out;

  D_Flip_Flop #(.trigger("falling")) d_ff_1 (.D(A2), .clk(clock_1_out), .Q(d_ff_1_q));  // open: Qn, preset, reset
  Clock clock_1 (.out(clock_1_out));
  D_Flip_Flop #(.trigger("falling")) d_ff_2 (.D(A1), .clk(clock_1_out), .Q(d_ff_2_q));  // open: Qn, preset, reset
  not not_1 (not_1_out, d_ff_3_q);
  not not_2 (not_2_out, d_ff_2_q);
  not not_3 (not_3_out, d_ff_2_q);
  not not_4 (not_4_out, d_ff_3_q);
  not not_5 (not_5_out, d_ff_1_q);
  not not_6 (not_6_out, d_ff_1_q);
  not not_7 (not_7_out, d_ff_3_q);
  not not_8 (not_8_out, d_ff_1_q);
  not not_9 (not_9_out, d_ff_2_q);
  not not_10 (not_10_out, d_ff_1_q);
  not not_11 (not_11_out, d_ff_2_q);
  not not_12 (not_12_out, d_ff_3_q);
  D_Flip_Flop #(.trigger("falling")) d_ff_3 (.D(A0), .clk(clock_1_out), .Q(d_ff_3_q));  // open: Qn, preset, reset
  and and_1 (and_1_out, d_ff_1_q, d_ff_2_q, clock_1_out, d_ff_3_q);
  and and_2 (and_2_out, and_1_out, not_13_out);
  and and_3 (and_3_out, d_ff_1_q, d_ff_2_q, clock_1_out, not_1_out);
  and and_4 (and_4_out, and_3_out, not_13_out);
  and and_5 (and_5_out, d_ff_1_q, not_2_out, clock_1_out, d_ff_3_q);
  and and_6 (and_6_out, and_5_out, not_13_out);
  and and_7 (and_7_out, d_ff_1_q, not_3_out, clock_1_out, not_4_out);
  and and_8 (and_8_out, and_7_out, not_13_out);
  and and_9 (and_9_out, not_5_out, d_ff_2_q, clock_1_out, d_ff_3_q);
  and and_10 (and_10_out, and_9_out, not_13_out);
  and and_11 (and_11_out, not_6_out, d_ff_2_q, clock_1_out, not_7_out);
  and and_12 (and_12_out, and_11_out, not_13_out);
  and and_13 (and_13_out, not_8_out, not_9_out, clock_1_out, d_ff_3_q);
  and and_14 (and_14_out, and_13_out, not_13_out);
  and and_15 (and_15_out, not_10_out, not_11_out, clock_1_out, not_12_out);
  and and_16 (and_16_out, and_15_out, not_13_out);
  D_Flip_Flop #(.trigger("falling")) d_ff_4 (.D(Mode), .clk(clock_1_out), .Q(d_ff_4_q));  // open: Qn, preset, reset
  not not_13 (not_13_out, d_ff_4_q);
  and and_17 (and_17_out, and_1_out, not_13_out, d_ff_13_q);
  D_Flip_Flop #(.trigger("high")) d_ff_5 (.D(and_17_out), .clk(and_2_out), .Q(d_ff_5_q));  // open: Qn, preset, reset
  and and_18 (and_18_out, and_3_out, not_13_out, d_ff_13_q);
  D_Flip_Flop #(.trigger("high")) d_ff_6 (.D(and_18_out), .clk(and_4_out), .Q(d_ff_6_q));  // open: Qn, preset, reset
  and and_19 (and_19_out, and_5_out, not_13_out, d_ff_13_q);
  D_Flip_Flop #(.trigger("high")) d_ff_7 (.D(and_19_out), .clk(and_6_out), .Q(d_ff_7_q));  // open: Qn, preset, reset
  and and_20 (and_20_out, and_7_out, not_13_out, d_ff_13_q);
  D_Flip_Flop #(.trigger("high")) d_ff_8 (.D(and_20_out), .clk(and_8_out), .Q(d_ff_8_q));  // open: Qn, preset, reset
  and and_21 (and_21_out, and_9_out, not_13_out, d_ff_13_q);
  D_Flip_Flop #(.trigger("high")) d_ff_9 (.D(and_21_out), .clk(and_10_out), .Q(d_ff_9_q));  // open: Qn, preset, reset
  and and_22 (and_22_out, and_11_out, not_13_out, d_ff_13_q);
  D_Flip_Flop #(.trigger("high")) d_ff_10 (.D(and_22_out), .clk(and_12_out), .Q(d_ff_10_q));  // open: Qn, preset, reset
  and and_23 (and_23_out, and_13_out, not_13_out, d_ff_13_q);
  D_Flip_Flop #(.trigger("high")) d_ff_11 (.D(and_23_out), .clk(and_14_out), .Q(d_ff_11_q));  // open: Qn, preset, reset
  and and_24 (and_24_out, and_15_out, not_13_out, d_ff_13_q);
  D_Flip_Flop #(.trigger("high")) d_ff_12 (.D(and_24_out), .clk(and_16_out), .Q(bit3));  // open: Qn, preset, reset
  Clock clock_2 ();  // open: out
  or or_1 (or_1_out, and_25_out, and_26_out, and_27_out, and_28_out, and_29_out, and_30_out, and_31_out, and_32_out);
  and and_25 (and_25_out, d_ff_5_q, and_1_out, d_ff_4_q);
  and and_26 (and_26_out, d_ff_6_q, and_3_out, d_ff_4_q);
  and and_27 (and_27_out, d_ff_7_q, and_5_out, d_ff_4_q);
  and and_28 (and_28_out, d_ff_8_q, and_7_out, d_ff_4_q);
  and and_29 (and_29_out, d_ff_9_q, and_9_out, d_ff_4_q);
  and and_30 (and_30_out, d_ff_10_q, and_11_out, d_ff_4_q);
  and and_31 (and_31_out, d_ff_11_q, and_13_out, d_ff_4_q);
  and and_32 (and_32_out, bit3, and_15_out, d_ff_4_q);
  D_Flip_Flop #(.trigger("falling")) d_ff_13 (.D(D3), .clk(clock_1_out), .Q(d_ff_13_q));  // open: Qn, preset, reset
  D_Flip_Flop #(.trigger("falling")) d_ff_14 (.D(D2), .clk(clock_1_out), .Q(d_ff_14_q));  // open: Qn, preset, reset
  and and_33 (and_33_out, and_1_out, not_13_out, d_ff_14_q);
  D_Flip_Flop #(.trigger("high")) d_ff_15 (.D(and_33_out), .clk(and_2_out), .Q(d_ff_15_q));  // open: Qn, preset, reset
  and and_34 (and_34_out, and_3_out, not_13_out, d_ff_14_q);
  D_Flip_Flop #(.trigger("high")) d_ff_16 (.D(and_34_out), .clk(and_4_out), .Q(d_ff_16_q));  // open: Qn, preset, reset
  and and_35 (and_35_out, and_5_out, not_13_out, d_ff_14_q);
  D_Flip_Flop #(.trigger("high")) d_ff_17 (.D(and_35_out), .clk(and_6_out), .Q(d_ff_17_q));  // open: Qn, preset, reset
  and and_36 (and_36_out, and_7_out, not_13_out, d_ff_14_q);
  D_Flip_Flop #(.trigger("high")) d_ff_18 (.D(and_36_out), .clk(and_8_out), .Q(d_ff_18_q));  // open: Qn, preset, reset
  and and_37 (and_37_out, and_9_out, not_13_out, d_ff_14_q);
  D_Flip_Flop #(.trigger("high")) d_ff_19 (.D(and_37_out), .clk(and_10_out), .Q(d_ff_19_q));  // open: Qn, preset, reset
  and and_38 (and_38_out, and_11_out, not_13_out, d_ff_14_q);
  D_Flip_Flop #(.trigger("high")) d_ff_20 (.D(and_38_out), .clk(and_12_out), .Q(d_ff_20_q));  // open: Qn, preset, reset
  and and_39 (and_39_out, and_13_out, not_13_out, d_ff_14_q);
  D_Flip_Flop #(.trigger("high")) d_ff_21 (.D(and_39_out), .clk(and_14_out), .Q(d_ff_21_q));  // open: Qn, preset, reset
  and and_40 (and_40_out, and_15_out, not_13_out, d_ff_14_q);
  D_Flip_Flop #(.trigger("high")) d_ff_22 (.D(and_40_out), .clk(and_16_out), .Q(bit2));  // open: Qn, preset, reset
  D_Flip_Flop #(.trigger("falling")) d_ff_23 (.D(D1), .clk(clock_1_out), .Q(d_ff_23_q));  // open: Qn, preset, reset
  D_Flip_Flop #(.trigger("high")) d_ff_24 (.D(or_1_out), .clk(clock_1_out), .Q(d_ff_24_q));  // open: Qn, preset, reset
  or or_2 (or_2_out, and_41_out, and_42_out, and_43_out, and_44_out, and_45_out, and_46_out, and_47_out, and_48_out);
  and and_41 (and_41_out, d_ff_15_q, and_1_out, d_ff_4_q);
  and and_42 (and_42_out, d_ff_16_q, and_3_out, d_ff_4_q);
  and and_43 (and_43_out, d_ff_17_q, and_5_out, d_ff_4_q);
  and and_44 (and_44_out, d_ff_18_q, and_7_out, d_ff_4_q);
  and and_45 (and_45_out, d_ff_19_q, and_9_out, d_ff_4_q);
  and and_46 (and_46_out, d_ff_20_q, and_11_out, d_ff_4_q);
  and and_47 (and_47_out, d_ff_21_q, and_13_out, d_ff_4_q);
  and and_48 (and_48_out, bit2, and_15_out, d_ff_4_q);
  D_Flip_Flop #(.trigger("falling")) d_ff_25 (.D(D0), .clk(clock_1_out), .Q(d_ff_25_q));  // open: Qn, preset, reset
  D_Flip_Flop #(.trigger("high")) d_ff_26 (.D(or_2_out), .clk(clock_1_out), .Q(d_ff_26_q));  // open: Qn, preset, reset
  D_Flip_Flop #(.trigger("high")) d_ff_27 (.D(or_3_out), .clk(clock_1_out), .Q(d_ff_27_q));  // open: Qn, preset, reset
  and and_49 (and_49_out, and_1_out, not_13_out, d_ff_23_q);
  and and_50 (and_50_out, and_3_out, not_13_out, d_ff_23_q);
  and and_51 (and_51_out, and_5_out, not_13_out, d_ff_23_q);
  and and_52 (and_52_out, and_7_out, not_13_out, d_ff_23_q);
  and and_53 (and_53_out, and_9_out, not_13_out, d_ff_23_q);
  and and_54 (and_54_out, and_11_out, not_13_out, d_ff_23_q);
  and and_55 (and_55_out, and_13_out, not_13_out, d_ff_23_q);
  and and_56 (and_56_out, and_15_out, not_13_out, d_ff_23_q);
  D_Flip_Flop #(.trigger("high")) d_ff_28 (.D(or_4_out), .clk(clock_1_out), .Q(d_ff_28_q));  // open: Qn, preset, reset
  D_Flip_Flop #(.trigger("high")) d_ff_29 (.D(and_49_out), .clk(and_2_out), .Q(d_ff_29_q));  // open: Qn, preset, reset
  D_Flip_Flop #(.trigger("high")) d_ff_30 (.D(and_50_out), .clk(and_4_out), .Q(d_ff_30_q));  // open: Qn, preset, reset
  D_Flip_Flop #(.trigger("high")) d_ff_31 (.D(and_51_out), .clk(and_6_out), .Q(d_ff_31_q));  // open: Qn, preset, reset
  D_Flip_Flop #(.trigger("high")) d_ff_32 (.D(and_52_out), .clk(and_8_out), .Q(d_ff_32_q));  // open: Qn, preset, reset
  D_Flip_Flop #(.trigger("high")) d_ff_33 (.D(and_53_out), .clk(and_10_out), .Q(d_ff_33_q));  // open: Qn, preset, reset
  D_Flip_Flop #(.trigger("high")) d_ff_34 (.D(and_54_out), .clk(and_12_out), .Q(d_ff_34_q));  // open: Qn, preset, reset
  D_Flip_Flop #(.trigger("high")) d_ff_35 (.D(and_55_out), .clk(and_14_out), .Q(d_ff_35_q));  // open: Qn, preset, reset
  D_Flip_Flop #(.trigger("high")) d_ff_36 (.D(and_56_out), .clk(and_16_out), .Q(bit1));  // open: Qn, preset, reset
  or or_3 (or_3_out, and_57_out, and_58_out, and_59_out, and_60_out, and_61_out, and_62_out, and_63_out, and_64_out);
  and and_57 (and_57_out, d_ff_29_q, and_1_out, d_ff_4_q);
  and and_58 (and_58_out, d_ff_30_q, and_3_out, d_ff_4_q);
  and and_59 (and_59_out, d_ff_31_q, and_5_out, d_ff_4_q);
  and and_60 (and_60_out, d_ff_32_q, and_7_out, d_ff_4_q);
  and and_61 (and_61_out, d_ff_33_q, and_9_out, d_ff_4_q);
  and and_62 (and_62_out, d_ff_34_q, and_11_out, d_ff_4_q);
  and and_63 (and_63_out, d_ff_35_q, and_13_out, d_ff_4_q);
  and and_64 (and_64_out, bit1, and_15_out, d_ff_4_q);
  and and_65 (and_65_out, and_1_out, not_13_out, d_ff_25_q);
  D_Flip_Flop #(.trigger("high")) d_ff_37 (.D(and_65_out), .clk(and_2_out), .Q(d_ff_37_q));  // open: Qn, preset, reset
  and and_66 (and_66_out, and_3_out, not_13_out, d_ff_25_q);
  D_Flip_Flop #(.trigger("high")) d_ff_38 (.D(and_66_out), .clk(and_4_out), .Q(d_ff_38_q));  // open: Qn, preset, reset
  and and_67 (and_67_out, and_5_out, not_13_out, d_ff_25_q);
  D_Flip_Flop #(.trigger("high")) d_ff_39 (.D(and_67_out), .clk(and_6_out), .Q(d_ff_39_q));  // open: Qn, preset, reset
  and and_68 (and_68_out, and_7_out, not_13_out, d_ff_25_q);
  D_Flip_Flop #(.trigger("high")) d_ff_40 (.D(and_68_out), .clk(and_8_out), .Q(d_ff_40_q));  // open: Qn, preset, reset
  and and_69 (and_69_out, and_9_out, not_13_out, d_ff_25_q);
  D_Flip_Flop #(.trigger("high")) d_ff_41 (.D(and_69_out), .clk(and_10_out), .Q(d_ff_41_q));  // open: Qn, preset, reset
  and and_70 (and_70_out, and_11_out, not_13_out, d_ff_25_q);
  D_Flip_Flop #(.trigger("high")) d_ff_42 (.D(and_70_out), .clk(and_12_out), .Q(d_ff_42_q));  // open: Qn, preset, reset
  and and_71 (and_71_out, and_13_out, not_13_out, d_ff_25_q);
  D_Flip_Flop #(.trigger("high")) d_ff_43 (.D(and_71_out), .clk(and_14_out), .Q(d_ff_43_q));  // open: Qn, preset, reset
  and and_72 (and_72_out, and_15_out, not_13_out, d_ff_25_q);
  D_Flip_Flop #(.trigger("high")) d_ff_44 (.D(and_72_out), .clk(and_16_out), .Q(bit0));  // open: Qn, preset, reset
  or or_4 (or_4_out, and_73_out, and_74_out, and_75_out, and_76_out, and_77_out, and_78_out, and_79_out, and_80_out);
  and and_73 (and_73_out, d_ff_37_q, and_1_out, d_ff_4_q);
  and and_74 (and_74_out, d_ff_38_q, and_3_out, d_ff_4_q);
  and and_75 (and_75_out, d_ff_39_q, and_5_out, d_ff_4_q);
  and and_76 (and_76_out, d_ff_40_q, and_7_out, d_ff_4_q);
  and and_77 (and_77_out, d_ff_41_q, and_9_out, d_ff_4_q);
  and and_78 (and_78_out, d_ff_42_q, and_11_out, d_ff_4_q);
  and and_79 (and_79_out, d_ff_43_q, and_13_out, d_ff_4_q);
  and and_80 (and_80_out, bit0, and_15_out, d_ff_4_q);
  and and_81 (O3, enable, d_ff_24_q);
  and and_82 (O2, d_ff_26_q, enable);
  and and_83 (O1, d_ff_27_q, enable);
  and and_84 (O0, d_ff_28_q, enable);

  // Notes on the sheet:
  //   3-bit address input pins
  //   Mode input pin
  //   4-bit data input pins
  //   4-bit data output pins
endmodule

module CU2 (
  input  OP1,
  input  OP0,
  input  regIn,
  input  addressIn,
  output halt,
  output regOut,
  output addressOut,
  output PCen,
  output maren,
  output rammode,
  output mbren,
  output iren
);

  wire add, alus_1_o0, alus_1_o1, alus_1_o2, clk, load, not_1_out, not_2_out, not_3_out, not_4_out,
       not_5_out, not_6_out, not_7_out, not_8_out, not_9_out, not_10_out, not_11_out, not_12_out, not_13_out,
       not_14_out, not_15_out, out0, out1, out2, save, sub;

  Clock clock_1 (.out(clk));
  not not_1 (not_1_out, OP1);
  not not_2 (not_2_out, OP0);
  and and_1 (load, not_1_out, not_2_out);
  not not_3 (not_3_out, out2);
  not not_4 (not_4_out, out1);
  not not_5 (not_5_out, out0);
  not not_6 (not_6_out, out2);
  not not_7 (not_7_out, out1);
  not not_8 (not_8_out, out2);
  not not_9 (not_9_out, out0);
  not not_10 (not_10_out, OP0);
  and and_2 (add, OP1, not_10_out);
  and and_3 (maren, not_3_out, not_4_out, not_5_out, clk);
  and and_4 (mbren, not_6_out, not_7_out, out0, clk);
  and and_5 (iren, not_8_out, out1, not_9_out, clk);
  not not_11 (not_11_out, OP1);
  and and_6 (save, not_11_out, OP0);
  and and_7 (sub, OP1, OP0);
  and and_8 (halt, addressIn, regIn, OP0, OP1);
  not not_12 (not_12_out, 1'b1);
  not not_13 (not_13_out, 1'b1);
  not not_14 (not_14_out, 1'b1);
  not not_15 (not_15_out, 1'b1);
  reg3bits reg3bits_1 (
    .rw(1'b1), .enable(1'b1), .I2(alus_1_o2), .I1(alus_1_o1), .I0(alus_1_o0), .O2(out2), .O1(out1), .O0(out0));
  aluS alus_1 (
    .L3(not_12_out), .L2(not_13_out), .L1(not_14_out), .L0(1'b1), .R2(out2), .R1(out1), .R0(out0),
    .command_pin(not_15_out), .O2(alus_1_o2), .O1(alus_1_o1), .O0(alus_1_o0));  // open: R3, overflow_status_bit, zero_status_bit, negative_status_bit, O3

  assign addressOut = addressIn;
  assign PCen = maren;
  assign rammode = mbren;
  assign regOut = regIn;

  // Notes on the sheet:
  //   Load
  //   Add
  //   Save
endmodule

module CU (
  input  OP1,
  input  OP0,
  input  regIn,
  input  addressIn,
  output halt,
  output load,
  output addressOut,
  output maren,
  output rammode,
  output mbren,
  output PCen,
  output put,
  output save,
  output iren,
  output a,
  output operation,
  output s,
  output regOut,
  output enable
);

  wire add, alus_1_o0, alus_1_o1, alus_1_o2, and_4_out, and_5_out, and_6_out, and_7_out, and_9_out,
       and_14_out, and_15_out, and_16_out, and_17_out, and_18_out, and_19_out, and_20_out, and_21_out,
       and_23_out, and_24_out, and_26_out, and_27_out, clk, clock_1_out, not_1_out, not_2_out, not_3_out,
       not_4_out, not_5_out, not_6_out, not_7_out, not_8_out, not_9_out, not_10_out, not_11_out, not_12_out,
       not_13_out, not_14_out, not_15_out, not_16_out, not_17_out, not_18_out, not_19_out, not_20_out,
       not_21_out, not_22_out, not_23_out, not_24_out, not_25_out, not_26_out, not_27_out, not_28_out,
       not_29_out, not_30_out, not_31_out, not_32_out, not_33_out, not_34_out, not_35_out, not_36_out,
       not_37_out, not_38_out, not_39_out, or_1_out, or_3_out, or_7_out, or_8_out, or_11_out, out0, out1,
       out2, save_t, sub;

  Clock clock_1 (.out(clock_1_out));
  not not_1 (not_1_out, halt);
  and and_1 (clk, not_1_out, clock_1_out);
  not not_2 (not_2_out, OP1);
  not not_3 (not_3_out, OP0);
  and and_2 (load, not_2_out, not_3_out);
  not not_4 (not_4_out, out2);
  not not_5 (not_5_out, out1);
  not not_6 (not_6_out, out0);
  not not_7 (not_7_out, out2);
  not not_8 (not_8_out, out1);
  not not_9 (not_9_out, out2);
  not not_10 (not_10_out, out0);
  not not_11 (not_11_out, out2);
  not not_12 (not_12_out, OP0);
  and and_3 (add, OP1, not_12_out);
  and and_4 (and_4_out, not_4_out, not_5_out, not_6_out, clk);
  not not_13 (not_13_out, halt);
  and and_5 (and_5_out, not_7_out, not_8_out, out0, clk);
  and and_6 (and_6_out, not_9_out, out1, not_10_out, clk);
  and and_7 (and_7_out, not_11_out, out1, out0);
  and and_8 (PCen, and_4_out, not_13_out);
  and and_9 (and_9_out, and_5_out, not_14_out);
  not not_14 (not_14_out, halt);
  or or_1 (or_1_out, and_7_out, out2);
  not not_15 (not_15_out, OP1);
  and and_10 (save_t, not_15_out, OP0);
  and and_11 (sub, OP1, OP0);
  or or_2 (mbren, and_15_out, and_18_out, and_9_out);
  or or_3 (or_3_out, and_6_out, or_1_out);
  not not_16 (not_16_out, halt);
  and and_12 (iren, or_3_out, not_16_out);
  buf or_4 (maren, PCen);  // OR_Gate
  and and_13 (halt, addressIn, regIn, OP0, OP1);
  not not_17 (not_17_out, out2);
  not not_18 (not_18_out, out1);
  not not_19 (not_19_out, out0);
  not not_20 (not_20_out, out1);
  and and_14 (and_14_out, not_17_out, out1, out0, load);
  and and_15 (and_15_out, out2, not_18_out, not_19_out, load);
  and and_16 (and_16_out, out2, not_20_out, out0, load);
  not not_21 (not_21_out, out2);
  and and_17 (and_17_out, not_21_out, out1, out0, save_t);
  not not_22 (not_22_out, out1);
  and and_18 (and_18_out, out2, not_22_out, not_23_out, save_t);
  not not_23 (not_23_out, out0);
  not not_24 (not_24_out, out1);
  and and_19 (and_19_out, out2, not_24_out, out0, save_t);
  and and_20 (and_20_out, out2, out1, not_25_out, save_t);
  not not_25 (not_25_out, out0);
  and and_21 (and_21_out, out2, out1, not_26_out, add);
  not not_26 (not_26_out, out0);
  and and_22 (a, out2, out1, out0, add);
  not not_27 (not_27_out, out2);
  not not_28 (not_28_out, out1);
  and and_23 (and_23_out, not_27_out, not_28_out, not_29_out, add);
  not not_29 (not_29_out, out0);
  not not_30 (not_30_out, out2);
  and and_24 (and_24_out, not_30_out, out1, out0, sub);
  not not_31 (not_31_out, out1);
  and and_25 (s, out2, not_31_out, not_32_out, sub);
  not not_32 (not_32_out, out0);
  not not_33 (not_33_out, out1);
  and and_26 (and_26_out, out2, not_33_out, out0, sub);
  or or_5 (save, and_17_out, and_18_out);
  or or_6 (enable, and_18_out, and_20_out, and_19_out);
  or or_7 (or_7_out, and_21_out, a);
  or or_8 (or_8_out, and_24_out, s);
  not not_34 (not_34_out, 1'b1);
  not not_35 (not_35_out, 1'b1);
  not not_36 (not_36_out, 1'b1);
  or or_9 (operation, or_7_out, or_8_out);
  not not_37 (not_37_out, 1'b1);
  reg3bits reg3bits_1 (
    .rw(1'b1), .enable(1'b1), .I2(alus_1_o2), .I1(alus_1_o1), .I0(alus_1_o0), .O2(out2), .O1(out1), .O0(out0));
  not not_38 (not_38_out, and_23_out);
  or or_10 (put, and_16_out, operation);
  not not_39 (not_39_out, and_26_out);
  or or_11 (or_11_out, not_38_out, not_39_out);
  and and_27 (and_27_out, or_11_out, regIn);
  or or_12 (regOut, and_16_out, and_27_out);
  aluS alus_1 (
    .L3(not_34_out), .L2(not_35_out), .L1(not_36_out), .L0(1'b1), .R2(out2), .R1(out1), .R0(out0),
    .command_pin(not_37_out), .O2(alus_1_o2), .O1(alus_1_o1), .O0(alus_1_o0));  // open: R3, overflow_status_bit, zero_status_bit, negative_status_bit, O3

  assign addressOut = addressIn;
  assign rammode = enable;

  // Other names for the same wires on the sheet: stop = halt

  // Notes on the sheet:
  //   Load
  //   Add
  //   Save
  //   Fetch cycle
endmodule

module numbers (
  input  I3,
  input  I2,
  input  I1,
  input  I0,
  output fifteen,
  output fourteen,
  output thirteen,
  output twelve,
  output eleven,
  output ten,
  output nine,
  output eight,
  output seven,
  output six,
  output five,
  output four,
  output three,
  output two,
  output one,
  output zero
);

  wire not_1_out, not_2_out, not_3_out, not_4_out, not_5_out, not_6_out, not_7_out, not_8_out, not_9_out,
       not_10_out, not_11_out, not_12_out, not_13_out, not_14_out, not_15_out, not_16_out, not_17_out,
       not_18_out, not_19_out, not_20_out, not_21_out, not_22_out, not_23_out, not_24_out, not_25_out,
       not_26_out, not_27_out, not_28_out, not_29_out, not_30_out, not_31_out, not_32_out;

  and and_1 (fifteen, I3, I2, I1, I0);
  and and_2 (fourteen, I3, I2, I1, not_1_out);
  not not_1 (not_1_out, I0);
  and and_3 (thirteen, I3, I2, not_2_out, I0);
  not not_2 (not_2_out, I1);
  and and_4 (twelve, I3, I2, not_3_out, not_4_out);
  not not_3 (not_3_out, I1);
  not not_4 (not_4_out, I0);
  not not_5 (not_5_out, I2);
  and and_5 (eleven, I3, not_5_out, I1, I0);
  not not_6 (not_6_out, I2);
  and and_6 (ten, I3, not_6_out, I1, not_7_out);
  not not_7 (not_7_out, I0);
  not not_8 (not_8_out, I2);
  and and_7 (nine, I3, not_8_out, not_9_out, I0);
  not not_9 (not_9_out, I1);
  not not_10 (not_10_out, I2);
  and and_8 (eight, I3, not_10_out, not_11_out, not_12_out);
  not not_11 (not_11_out, I1);
  not not_12 (not_12_out, I0);
  not not_13 (not_13_out, I3);
  and and_9 (seven, not_13_out, I2, I1, I0);
  not not_14 (not_14_out, I3);
  and and_10 (six, not_14_out, I2, I1, not_15_out);
  not not_15 (not_15_out, I0);
  not not_16 (not_16_out, I3);
  and and_11 (five, not_16_out, I2, not_17_out, I0);
  not not_17 (not_17_out, I1);
  not not_18 (not_18_out, I3);
  and and_12 (four, not_18_out, I2, not_19_out, not_20_out);
  not not_19 (not_19_out, I1);
  not not_20 (not_20_out, I0);
  not not_21 (not_21_out, I3);
  not not_22 (not_22_out, I2);
  and and_13 (three, not_21_out, not_22_out, I1, I0);
  not not_23 (not_23_out, I3);
  not not_24 (not_24_out, I2);
  and and_14 (two, not_23_out, not_24_out, I1, not_25_out);
  not not_25 (not_25_out, I0);
  not not_26 (not_26_out, I3);
  not not_27 (not_27_out, I2);
  and and_15 (one, not_26_out, not_27_out, not_28_out, I0);
  not not_28 (not_28_out, I1);
  not not_29 (not_29_out, I3);
  not not_30 (not_30_out, I2);
  and and_16 (zero, not_29_out, not_30_out, not_31_out, not_32_out);
  not not_31 (not_31_out, I1);
  not not_32 (not_32_out, I0);
endmodule
